# Fritzing sketch Stage_0 (saved by Fritzing 0.9.9b)
breadboards: 1

parts:
  Q1 = Basic FET N-Channel [package="TO220 [THT]"]
  J1 = Camdenboss CTB0158-4 [part_number=CTB0158-4 package=THT]
  J2 = Camdenboss CTB0158-4 [part_number=CTB0158-4 package=THT]
  C4 = Electrolytic Capacitor [capacitance=1µF voltage=35V package="100 mil [THT, electrolytic]"]
  R6 = Resistor [tolerance=±1% resistance=22k power=0.25 package="0402 [SMD]"]
  R7 = Resistor [tolerance=±1% resistance=15k power=0.25 package="0603 [SMD]"]
  IC1 = IC, DIP package, 8 pins [chip_label=LTC4367]
  Q2 = Basic FET N-Channel [package="TO220 [THT]"]
  R8 = Resistor [tolerance=±1% resistance=22k power=0.25 package="0402 [SMD]"]
  R9 = Resistor [tolerance=±1% resistance=15k power=0.25 package="0603 [SMD]"]
  R10 = Resistor [tolerance=±5% power=0.25 resistance=220 package=THT]
  LED1 = LED - 5mm [color="Red (633nm)" current=0.030 package="5 mm [THT]"]

nets:
  N1: Q1.gate, IC1.pin8, Q2.gate
  N2: Q1.drain, J1.pin1, J1.pin2, IC1.pin1, R8.Pin_0
  N3: Q1.source, Q2.source
  GND: J1.pin3, J1.pin4, J2.pin3, J2.pin4, C4.-, IC1.pin4, R9.Pin_1
  N4: J2.pin1, J2.pin2, C4.+, IC1.pin7, Q2.drain, R10.Pin_0
  N5: R6.Pin_0, IC1.pin5, R8.Pin_1
  N6: R6.Pin_1, R7.Pin_0, IC1.pin2
  N7: R7.Pin_1, IC1.pin3, R9.Pin_0
  N8: IC1.pin6, LED1.cathode
  N9: R10.Pin_1, LED1.anode
