# Fritzing sketch Stage_1 (saved by Fritzing 0.9.9b)
perfboards: 1

parts:
  IC1 = IC, DIP package, 10 pins [chip_label=LT3757]
  Q1 = Basic FET N-Channel [package="TO220 [THT]"]
  L1 = Inductor [package="400 mil [THT]"]
  D1 = Rectifier Diode [part_number=1N4001 package="300 mil [THT]"]
  R1 = Resistor [tolerance=±5% power=0.25 resistance=220 package=THT]
  R2 = Resistor [tolerance=±5% power=0.25 resistance=220 package=THT]
  C1 = Ceramic Capacitor [capacitance=100nF voltage=35V package="100 mil [THT, multilayer]"]
  R3 = Resistor [tolerance=±5% power=0.25 resistance=220 package=THT]
  C2 = Ceramic Capacitor [capacitance=100nF voltage=35V package="100 mil [THT, multilayer]"]
  R4 = Resistor [tolerance=±5% power=0.25 resistance=220 package=THT]
  C3 = Ceramic Capacitor [capacitance=100nF voltage=35V package="100 mil [THT, multilayer]"]
  R5 = Resistor [tolerance=±5% power=0.25 resistance=220 package=THT]
  J1 = Camdenboss CTB0158-4 [part_number=CTB0158-4 package=THT]
  J2 = Camdenboss CTB0158-4 [part_number=CTB0158-4 package=THT]
  C4 = Electrolytic Capacitor [capacitance=1µF voltage=35V package="100 mil [THT, electrolytic]"]
  R6 = Resistor [tolerance=±5% resistance=220 power=0.25 package="0402 [SMD]"]
  R7 = Resistor [tolerance=±5% resistance=220 power=0.25 package="0603 [SMD]"]

nets:
  N1: IC1.pin1, R3.Pin_1
  N2: IC1.pin2, R1.Pin_0, R2.Pin_1
  N3: IC1.pin3, C3.1
  N4: IC1.pin4, R4.Pin_0
  GND: IC1.pin5, R2.Pin_0, C1.0, C2.0, R4.Pin_1, C3.0, R5.Pin_0, J1.pin3, J1.pin4, J2.pin3, J2.pin4, C4.-, R7.Pin_1
  N5: IC1.pin6, Q1.source, R5.Pin_1
  N6: IC1.pin7, Q1.gate
  N7: IC1.pin8, C1.1
  N8: IC1.pin9, R6.Pin_1, R7.Pin_0
  N9: IC1.pin10, L1.pin_0, J1.pin1, J1.pin2, R6.Pin_0
  N10: Q1.drain, L1.pin_1, D1.anode
  N11: D1.cathode, R1.Pin_1, J2.pin1, J2.pin2, C4.+
  N12: R3.Pin_0, C2.1
