# Fritzing sketch Stage_2 (saved by Fritzing 0.9.9b)
perfboards: 1

parts:
  R1 = Resistor [tolerance=±5% power=0.25 resistance=22k package=THT]
  R2 = Resistor [tolerance=±1% power=0.25 resistance=1.5k package=THT]
  J1 = Camdenboss CTB0158-4 [part_number=CTB0158-4 package=THT]
  J2 = Camdenboss CTB0158-4 [part_number=CTB0158-4 package=THT]
  C4 = Electrolytic Capacitor [capacitance=1µF voltage=35V package="100 mil [THT, electrolytic]"]
  IC1 = IC, DIP package, 16 pins [chip_label=LT3724]
  Q1 = Basic FET N-Channel [package="TO220 [THT]"]
  L1 = Inductor [package="400 mil [THT]"]
  R3 = Resistor [tolerance=±5% power=0.25 resistance=220 package=THT]
  D1 = Rectifier Diode [part_number=1N4001 package="300 mil [THT]"]
  R4 = Resistor [tolerance=±5% power=0.25 resistance=220 package=THT]
  D2 = Rectifier Diode [part_number=1N4001 package="300 mil [THT]"]
  C5 = Ceramic Capacitor [capacitance=100nF voltage=35V package="100 mil [THT, multilayer]"]
  C6 = Ceramic Capacitor [capacitance=100nF voltage=35V package="100 mil [THT, multilayer]"]
  C7 = Ceramic Capacitor [capacitance=100nF voltage=35V package="100 mil [THT, multilayer]"]
  R5 = Resistor [tolerance=±5% power=0.25 resistance=220 package=THT]
  R6 = Resistor [tolerance=±5% power=0.25 resistance=220 package=THT]
  C8 = Ceramic Capacitor [capacitance=100nF voltage=35V package="100 mil [THT, multilayer]"]
  R7 = Resistor [tolerance=±5% power=0.25 resistance=220 package=THT]
  R8 = Resistor [tolerance=±5% power=0.25 resistance=220 package=THT]
  D3 = Rectifier Diode [part_number=1N4001 package="300 mil [THT]"]
  C9 = Electrolytic Capacitor [capacitance=1µF voltage=35V package="100 mil [THT, electrolytic]"]

nets:
  N1: R1.Pin_0, R2.Pin_1, IC1.pin6
  N2: R1.Pin_1, J2.pin1, J2.pin2, C4.+, IC1.pin9, R4.Pin_1
  GND: R2.Pin_0, J1.pin3, J1.pin4, J2.pin3, J2.pin4, C4.-, IC1.pin5, IC1.pin8, D1.anode, C6.0, C7.0, C8.0, R8.Pin_0, C9.-
  N3: J1.pin1, J1.pin2, IC1.pin1, Q1.drain, R7.Pin_1, D3.anode
  N4: IC1.pin3, R7.Pin_0, R8.Pin_1
  N5: IC1.pin4, R6.Pin_1
  N6: IC1.pin7, C6.1, R5.Pin_1
  N7: IC1.pin10, L1.pin_1, D1.cathode, R4.Pin_0, C5.0
  N8: IC1.pin12, D2.anode
  N9: IC1.pin14, R3.Pin_1
  N10: IC1.pin15, Q1.gate
  N11: IC1.pin16, D2.cathode, C5.1
  N12: Q1.source, L1.pin_0, R3.Pin_0
  N13: C7.1, R5.Pin_0
  N14: R6.Pin_0, C8.1
  N15: D3.cathode, C9.+
